# Fritzing sketch motion_nightlight_100 (saved by Fritzing 0.9.1b)
breadboards: 1

parts:
  Q1 = TIP120 Hi-Current Darlington Transistor
  USB-Boarduino_v2_1 = Boarduino
  PIR1 = PIR sensor
  LED1 = LED - 3mm [color="Red (633nm)" package="3 mm [THT]"]
  R1 = Resistor [tolerance=±5% resistance=220 package="0603 [SMD]"]
  R2 = Resistor [tolerance=±5% resistance=220 package="1206 [SMD]"]
  LED2 = LED - 5mm [color="Red (633nm)" package="5 mm [THT]"]
  R3 = Resistor [package="2512 [SMD]"]
  proto1 = Adafruit_PermaProto_1_4_Board
  R4 = Resistor [tolerance=±5% resistance=220 package="0603 [SMD]"]  # not connected
  R5 = Resistor [tolerance=±5% resistance=220 package="0603 [SMD]"]  # not connected
  R6 = Resistor [tolerance=±5% resistance=220 package="0603 [SMD]"]  # not connected
  R7 = Resistor [tolerance=±5% resistance=220 package="0603 [SMD]"]  # not connected
  R8 = Resistor [tolerance=±5% resistance=220 package="0603 [SMD]"]  # not connected
  LED3 = LED - 5mm [color="Red (633nm)" package="5 mm [THT]"]  # not connected
  LED4 = LED - 5mm [color="Red (633nm)" package="5 mm [THT]"]  # not connected
  LED5 = LED - 5mm [color="Red (633nm)" package="5 mm [THT]"]  # not connected
  LED6 = LED - 5mm [color="Red (633nm)" package="5 mm [THT]"]  # not connected
  LED7 = LED - 5mm [color="Red (633nm)" package="5 mm [THT]"]  # not connected

nets:
  N1: Q1.BASE, R3.Pin_1
  VCC: Q1.COLLECTOR, USB-Boarduino_v2_1.Vcc, PIR1.VDD
  N2: Q1.EMITTER, proto1.connectorW13
  GND: USB-Boarduino_v2_1.gnd, PIR1.GND, R1.Pin_1, R2.Pin_1, proto1.connectorZ15
  N3: USB-Boarduino_v2_1.d4, LED1.anode
  N4: USB-Boarduino_v2_1.d5, R3.Pin_0
  N5: USB-Boarduino_v2_1.d6, PIR1.SIG
  N6: USB-Boarduino_v2_1.d13, LED2.anode
  N7: LED1.cathode, R1.Pin_0
  N8: R2.Pin_0, LED2.cathode
  N9: proto1.connectorC3, proto1.connectorW3
  N10: proto1.connectorC6, proto1.connectorW6
  N11: proto1.connectorC9, proto1.connectorW9
  N12: proto1.connectorC12, proto1.connectorW12
  N13: proto1.connectorC15, proto1.connectorW15
  N14: proto1.connectorH2, proto1.connectorZ2
  N15: proto1.connectorH5, proto1.connectorZ5
  N16: proto1.connectorH8, proto1.connectorZ8
  N17: proto1.connectorH11, proto1.connectorZ11
  N18: proto1.connectorH14, proto1.connectorZ14

notes:
  1K resistor
  Vin to TIP120 is high mA source.
  Vcc is Vin on DC Boarduino. This must be a high mA source to drive the LED panel.
