# Fritzing sketch motion_nightlight_101 (saved by Fritzing 0.9.3b)
breadboards: 1

parts:
  Q1 = TIP120 Hi-Current Darlington Transistor
  USB-Boarduino_v2_1 = Boarduino
  PIR1 = PIR sensor
  LED1 = LED - 3mm [color="Red (633nm)" package="3 mm [THT]"]
  R1 = Resistor [tolerance=±5% resistance=220 package="0603 [SMD]"]
  R2 = Resistor [tolerance=±5% resistance=220 package="1206 [SMD]"]
  LED2 = LED - 5mm [color="Red (633nm)" package="5 mm [THT]"]
  R4 = Resistor [tolerance=±5% resistance=220 package="0603 [SMD]"]  # not connected
  R5 = Resistor [tolerance=±5% resistance=220 package="0603 [SMD]"]  # not connected
  R6 = Resistor [tolerance=±5% resistance=220 package="0603 [SMD]"]  # not connected
  R7 = Resistor [tolerance=±5% resistance=220 package="0603 [SMD]"]  # not connected
  R8 = Resistor [tolerance=±5% resistance=220 package="0603 [SMD]"]  # not connected
  LED3 = LED - 5mm [color="Red (633nm)" package="5 mm [THT]"]  # not connected
  LED4 = LED - 5mm [color="Red (633nm)" package="5 mm [THT]"]  # not connected
  LED5 = LED - 5mm [color="Red (633nm)" package="5 mm [THT]"]  # not connected
  LED6 = LED - 5mm [color="Red (633nm)" package="5 mm [THT]"]  # not connected
  LED7 = LED - 5mm [color="Red (633nm)" package="5 mm [THT]"]  # not connected
  R3 = Resistor [tolerance=±5% resistance=220 package="2512 [SMD]"]
  R9 = Photocell (LDR) [package=THT]
  R10 = Resistor [tolerance=±5% resistance=220 package=THT]

nets:
  N1: Q1.BASE, R3.Pin_1
  VCC: Q1.COLLECTOR, USB-Boarduino_v2_1.Vcc, PIR1.VDD, R9.pin_0
  GND: USB-Boarduino_v2_1.gnd, PIR1.GND, R1.Pin_1, R2.Pin_1, R10.Pin_1
  N2: USB-Boarduino_v2_1.d4, LED1.anode
  N3: USB-Boarduino_v2_1.d5, R3.Pin_0
  N4: USB-Boarduino_v2_1.d6, PIR1.SIG
  N5: USB-Boarduino_v2_1.d13, LED2.anode
  N6: USB-Boarduino_v2_1.a2, R9.pin_1, R10.Pin_0
  N7: LED1.cathode, R1.Pin_0
  N8: R2.Pin_0, LED2.cathode

notes:
  1K resistor
  Vin to TIP120 is high mA source.
  Vcc is Vin on DC Boarduino. This must be a high mA source to drive the LED panel.
